// Logisim project Piloufas.circ as structural Verilog: 7 circuits, main circuit main
module main (
);

  wire button_1_out, button_2_out, button_3_out, button_4_out;
  wire [3:0] output_display_1_o, output_display_1_o_2;
  wire [23:0] clocker_1_o;
  wire [23:8] output_display_1_o_3;

  Button button_1 (.out(button_1_out));
  Button button_2 (.out(button_2_out));
  Button button_3 (.out(button_3_out));
  Button button_4 (.out(button_4_out));
  button_input button_input_1 (
    .A(button_1_out), .B(button_2_out), .C(button_3_out), .R(button_4_out));  // open: A_st, A_lg, B_st, B_lg, C_st, C_lg
  clocker clocker_1 (.EN(1'b1), .o(clocker_1_o));  // open: R
  output_display output_display_1 (
    .i_1(clocker_1_o), .o({output_display_1_o_3, output_display_1_o_2, output_display_1_o}));  // open: i_2, i_3, i_4, nxt, R
  Hex_Digit_Display hex_digit_display_1 (.value(output_display_1_o_3[23:20]));  // open: dp
  Hex_Digit_Display hex_digit_display_2 (.value(output_display_1_o_3[19:16]));  // open: dp
  Hex_Digit_Display hex_digit_display_3 (.value(output_display_1_o_3[11:8]));  // open: dp
  Hex_Digit_Display hex_digit_display_4 (.value(output_display_1_o_3[15:12]));  // open: dp
  Hex_Digit_Display hex_digit_display_5 (.value(output_display_1_o_2));  // open: dp
  Hex_Digit_Display hex_digit_display_6 (.value(output_display_1_o));  // open: dp
endmodule

module press (
  input  b_in,
  input  R,
  output st,
  output lg
);

  wire clock_1_out, counter_1_carry, counter_2_carry, d_ff_1_q, d_ff_2_q, not_1_out, not_2_out, not_3_out,
       or_1_out, or_2_out, or_3_out, or_4_out;

  Clock clock_1 (.out(clock_1_out));
  D_Flip_Flop #(.trigger("falling")) d_ff_1 (
    .D(not_1_out), .clk(b_in), .Q(d_ff_1_q), .reset(or_3_out));  // open: Qn, preset
  not not_1 (not_1_out, counter_1_carry);
  D_Flip_Flop #(.trigger("falling")) d_ff_2 (
    .D(counter_1_carry), .clk(b_in), .Q(d_ff_2_q), .reset(or_3_out));  // open: Qn, preset
  or or_1 (or_1_out, counter_2_carry, R);
  or or_2 (or_2_out, b_in, R);
  or or_3 (or_3_out, R, counter_2_carry);
  Counter #(.width(2), .max('h3), .ongoal("stay")) counter_1 (
    .clr(or_1_out), .count(b_in), .clk(clock_1_out), .carry(counter_1_carry));  // open: load, up, D, Q
  Counter #(.width(2), .max('h3), .ongoal("stay")) counter_2 (
    .clr(or_2_out), .count(or_4_out), .clk(clock_1_out), .carry(counter_2_carry));  // open: load, up, D, Q
  or or_4 (or_4_out, d_ff_1_q, d_ff_2_q);
  not not_2 (not_2_out, counter_1_carry);
  not not_3 (not_3_out, d_ff_1_q);
  and and_1 (st, d_ff_1_q, not_2_out);
  and and_2 (lg, counter_1_carry, not_3_out);
endmodule

module button_input (
  input  A,
  input  B,
  input  C,
  input  R,
  output A_st,
  output A_lg,
  output B_st,
  output B_lg,
  output C_st,
  output C_lg
);

  press press_1 (.b_in(A), .R(R), .st(A_st), .lg(A_lg));
  press press_2 (.b_in(B), .R(R), .st(B_st), .lg(B_lg));
  press press_3 (.b_in(C), .R(R), .st(C_st), .lg(C_lg));
endmodule

module output_display (
  input  [23:0] i_1,
  input  [23:0] i_2,
  input  [23:0] i_3,
  input  [23:0] i_4,
  input  nxt,
  input  R,
  output [23:0] o
);

  wire clock_1_out;
  wire [1:0] counter_1_q;

  Clock clock_1 (.out(clock_1_out));
  Counter #(.width(2), .max('h3)) counter_1 (
    .clr(R), .count(nxt), .clk(clock_1_out), .Q(counter_1_q));  // open: load, up, D, carry
  Multiplexer #(.select(2), .width(24), .enable("false")) multiplexer_1 (
    .in0(i_1), .in1(i_2), .in2(i_3), .in3(i_4), .out(o), .sel(counter_1_q));
endmodule

module count_to_sixty (
  input  EN,
  input  R,
  output [3:0] low,
  output [3:0] high,
  output c
);

  wire and_1_out, clock_1_out, counter_1_carry, counter_2_carry;

  Clock clock_1 (.out(clock_1_out));
  Counter #(.width(4), .max('h9)) counter_1 (
    .clr(R), .count(EN), .clk(clock_1_out), .carry(counter_1_carry), .Q(low));  // open: load, up, D
  Counter #(.width(4), .max('h5)) counter_2 (
    .clr(R), .count(and_1_out), .clk(clock_1_out), .carry(counter_2_carry), .Q(high));  // open: load, up, D
  and and_1 (and_1_out, counter_1_carry, EN);
  and and_2 (c, counter_2_carry, and_1_out);
endmodule

module count_to_twenty (
  input  EN,
  input  R,
  output [3:0] low,
  output [3:0] high
);

  wire and_1_out, and_2_out, clock_1_out, comparator_1_eq, counter_1_carry, counter_2_carry, or_1_out;

  Clock clock_1 (.out(clock_1_out));
  or or_1 (or_1_out, R, and_2_out);
  Counter #(.width(4), .max('h9)) counter_1 (
    .clr(or_1_out), .count(EN), .clk(clock_1_out), .carry(counter_1_carry), .Q(low));  // open: load, up, D
  Counter #(.width(4), .max('h2)) counter_2 (
    .clr(or_1_out), .count(and_1_out), .clk(clock_1_out), .carry(counter_2_carry), .Q(high));  // open: load, up, D
  and and_1 (and_1_out, counter_1_carry, EN);
  Comparator #(.width(4)) comparator_1 (.a(low), .b(4'b0100), .eq(comparator_1_eq));  // open: gt, lt
  and and_2 (and_2_out, comparator_1_eq, counter_2_carry);
endmodule

module clocker (
  input  EN,
  input  R,
  output [23:0] o
);

  wire count_to_sixty_1_c, count_to_sixty_2_c;

  count_to_sixty count_to_sixty_1 (.EN(EN), .R(R), .low(o[3:0]), .high(o[7:4]), .c(count_to_sixty_1_c));
  count_to_sixty count_to_sixty_2 (
    .EN(count_to_sixty_1_c), .R(R), .low(o[11:8]), .high(o[15:12]), .c(count_to_sixty_2_c));
  count_to_twenty count_to_twenty_1 (.EN(count_to_sixty_2_c), .R(R), .low(o[19:16]), .high(o[23:20]));
endmodule
