// Logisim project piloufasV2.circ as structural Verilog
module main (
);

  wire B_out;

  Clock sysclk ();  // open: out
  Button B (.out(B_out));
  seven second_low ();  // open: Input_bus_1, cen, l_h, top, r_h, r_b, bot, l_b
endmodule

module count_10 (
  input  EN,
  input  R,
  output [3:0] data_o,
  output c_out
);

  wire and_1_out, and_2_out, clock_1_out, or_1_out;

  Clock clock_1 (.out(clock_1_out));
  or or_1 (or_1_out, R, c_out);
  J_K_Flip_Flop j_k_ff_1 (.J(EN), .K(EN), .clk(clock_1_out), .Q(data_o[0]), .reset(or_1_out));  // open: Qn, preset
  J_K_Flip_Flop j_k_ff_2 (
    .J(data_o[0]), .K(data_o[0]), .clk(clock_1_out), .Q(data_o[1]), .reset(or_1_out));  // open: Qn, preset
  and and_1 (and_1_out, data_o[0], data_o[1]);
  J_K_Flip_Flop j_k_ff_3 (
    .J(and_1_out), .K(and_1_out), .clk(clock_1_out), .Q(data_o[2]), .reset(or_1_out));  // open: Qn, preset
  and and_2 (and_2_out, data_o[2], and_1_out);
  J_K_Flip_Flop j_k_ff_4 (
    .J(and_2_out), .K(and_2_out), .clk(clock_1_out), .Q(data_o[3]), .reset(or_1_out));  // open: Qn, preset
  and and_3 (c_out, data_o[1], data_o[3]);
endmodule

module divide_128 (
);

  wire clock_1_out, d_ff_1_q, d_ff_2_q, d_ff_3_q, d_ff_4_q, d_ff_5_q, d_ff_6_q, d_ff_7_q, d_ff_8_q, d_ff_9_q,
       d_ff_10_q, d_ff_11_q, d_ff_12_q, d_ff_13_q, d_ff_14_q, d_ff_15_q, d_ff_16_q, d_ff_17_q, d_ff_18_q,
       d_ff_19_q, d_ff_20_q, d_ff_21_q, d_ff_22_q, d_ff_23_q, d_ff_24_q, d_ff_25_q, d_ff_26_q, d_ff_27_q,
       d_ff_28_q, d_ff_29_q, d_ff_30_q, d_ff_31_q, d_ff_32_q, d_ff_33_q, d_ff_34_q, d_ff_35_q, d_ff_36_q,
       d_ff_37_q, d_ff_38_q, d_ff_39_q, d_ff_40_q, d_ff_41_q, d_ff_42_q, d_ff_43_q, d_ff_44_q, d_ff_45_q,
       d_ff_46_q, d_ff_47_q, d_ff_48_q, d_ff_49_q, d_ff_50_q, d_ff_51_q, d_ff_52_q, d_ff_53_q, d_ff_54_q,
       d_ff_55_q, d_ff_56_q, d_ff_57_q, d_ff_58_q, d_ff_59_q, d_ff_60_q, d_ff_61_q, d_ff_62_q, d_ff_63_q,
       d_ff_64_q, d_ff_65_q, d_ff_66_q, d_ff_67_q, d_ff_68_q, d_ff_69_q, d_ff_70_q, d_ff_71_q, d_ff_72_q,
       d_ff_73_q, d_ff_74_q, d_ff_75_q, d_ff_76_q, d_ff_77_q, d_ff_78_q, d_ff_79_q, d_ff_80_q, d_ff_81_q,
       d_ff_82_q, d_ff_83_q, d_ff_84_q, d_ff_85_q, d_ff_86_q, d_ff_87_q, d_ff_88_q, d_ff_89_q, d_ff_90_q,
       d_ff_91_q, d_ff_92_q, d_ff_93_q, d_ff_94_q, d_ff_95_q, d_ff_96_q, d_ff_97_q, d_ff_98_q, d_ff_99_q,
       d_ff_100_q, d_ff_101_q, d_ff_102_q, d_ff_103_q, d_ff_104_q, d_ff_105_q, d_ff_106_q, d_ff_107_q,
       d_ff_108_q, d_ff_109_q, d_ff_110_q, d_ff_111_q, d_ff_112_q, d_ff_113_q, d_ff_114_q, d_ff_115_q,
       d_ff_116_q, d_ff_117_q, d_ff_118_q, d_ff_119_q, d_ff_120_q, d_ff_121_q, d_ff_122_q, d_ff_123_q,
       d_ff_124_q, d_ff_125_q, d_ff_126_q, d_ff_127_q, d_ff_128_qn, r;

  D_Flip_Flop d_ff_1 (.D(d_ff_128_qn), .clk(clock_1_out), .Q(d_ff_1_q));  // open: Qn, preset, reset
  D_Flip_Flop d_ff_2 (.D(d_ff_49_q), .clk(clock_1_out), .Q(d_ff_2_q), .reset(r));  // open: Qn, preset
  D_Flip_Flop d_ff_3 (.D(d_ff_50_q), .clk(clock_1_out), .Q(d_ff_3_q), .reset(r));  // open: Qn, preset
  D_Flip_Flop d_ff_4 (.D(d_ff_51_q), .clk(clock_1_out), .Q(d_ff_4_q), .reset(r));  // open: Qn, preset
  D_Flip_Flop d_ff_5 (.D(d_ff_52_q), .clk(clock_1_out), .Q(d_ff_5_q), .reset(r));  // open: Qn, preset
  D_Flip_Flop d_ff_6 (.D(d_ff_53_q), .clk(clock_1_out), .Q(d_ff_6_q), .reset(r));  // open: Qn, preset
  D_Flip_Flop d_ff_7 (.D(d_ff_54_q), .clk(clock_1_out), .Q(d_ff_7_q), .reset(r));  // open: Qn, preset
  D_Flip_Flop d_ff_8 (.D(d_ff_55_q), .clk(clock_1_out), .Q(d_ff_8_q), .reset(r));  // open: Qn, preset
  D_Flip_Flop d_ff_9 (.D(d_ff_56_q), .clk(clock_1_out), .Q(d_ff_9_q), .reset(r));  // open: Qn, preset
  D_Flip_Flop d_ff_10 (.D(d_ff_57_q), .clk(clock_1_out), .Q(d_ff_10_q), .reset(r));  // open: Qn, preset
  D_Flip_Flop d_ff_11 (.D(d_ff_58_q), .clk(clock_1_out), .Q(d_ff_11_q), .reset(r));  // open: Qn, preset
  D_Flip_Flop d_ff_12 (.D(d_ff_59_q), .clk(clock_1_out), .Q(d_ff_12_q), .reset(r));  // open: Qn, preset
  D_Flip_Flop d_ff_13 (.D(d_ff_60_q), .clk(clock_1_out), .Q(d_ff_13_q), .reset(r));  // open: Qn, preset
  D_Flip_Flop d_ff_14 (.D(d_ff_61_q), .clk(clock_1_out), .Q(d_ff_14_q), .reset(r));  // open: Qn, preset
  D_Flip_Flop d_ff_15 (.D(d_ff_62_q), .clk(clock_1_out), .Q(d_ff_15_q), .reset(r));  // open: Qn, preset
  D_Flip_Flop d_ff_16 (.D(d_ff_63_q), .clk(clock_1_out), .Q(d_ff_16_q), .reset(r));  // open: Qn, preset
  D_Flip_Flop d_ff_17 (.D(d_ff_1_q), .clk(clock_1_out), .Q(d_ff_17_q), .reset(r));  // open: Qn, preset
  D_Flip_Flop d_ff_18 (.D(d_ff_2_q), .clk(clock_1_out), .Q(d_ff_18_q), .reset(r));  // open: Qn, preset
  D_Flip_Flop d_ff_19 (.D(d_ff_3_q), .clk(clock_1_out), .Q(d_ff_19_q), .reset(r));  // open: Qn, preset
  D_Flip_Flop d_ff_20 (.D(d_ff_4_q), .clk(clock_1_out), .Q(d_ff_20_q), .reset(r));  // open: Qn, preset
  D_Flip_Flop d_ff_21 (.D(d_ff_5_q), .clk(clock_1_out), .Q(d_ff_21_q), .reset(r));  // open: Qn, preset
  D_Flip_Flop d_ff_22 (.D(d_ff_6_q), .clk(clock_1_out), .Q(d_ff_22_q), .reset(r));  // open: Qn, preset
  D_Flip_Flop d_ff_23 (.D(d_ff_7_q), .clk(clock_1_out), .Q(d_ff_23_q), .reset(r));  // open: Qn, preset
  D_Flip_Flop d_ff_24 (.D(d_ff_8_q), .clk(clock_1_out), .Q(d_ff_24_q), .reset(r));  // open: Qn, preset
  D_Flip_Flop d_ff_25 (.D(d_ff_9_q), .clk(clock_1_out), .Q(d_ff_25_q), .reset(r));  // open: Qn, preset
  D_Flip_Flop d_ff_26 (.D(d_ff_10_q), .clk(clock_1_out), .Q(d_ff_26_q), .reset(r));  // open: Qn, preset
  D_Flip_Flop d_ff_27 (.D(d_ff_11_q), .clk(clock_1_out), .Q(d_ff_27_q), .reset(r));  // open: Qn, preset
  D_Flip_Flop d_ff_28 (.D(d_ff_12_q), .clk(clock_1_out), .Q(d_ff_28_q), .reset(r));  // open: Qn, preset
  D_Flip_Flop d_ff_29 (.D(d_ff_13_q), .clk(clock_1_out), .Q(d_ff_29_q), .reset(r));  // open: Qn, preset
  D_Flip_Flop d_ff_30 (.D(d_ff_14_q), .clk(clock_1_out), .Q(d_ff_30_q), .reset(r));  // open: Qn, preset
  D_Flip_Flop d_ff_31 (.D(d_ff_15_q), .clk(clock_1_out), .Q(d_ff_31_q), .reset(r));  // open: Qn, preset
  D_Flip_Flop d_ff_32 (.D(d_ff_16_q), .clk(clock_1_out), .Q(d_ff_32_q), .reset(r));  // open: Qn, preset
  D_Flip_Flop d_ff_33 (.D(d_ff_17_q), .clk(clock_1_out), .Q(d_ff_33_q), .reset(r));  // open: Qn, preset
  D_Flip_Flop d_ff_34 (.D(d_ff_18_q), .clk(clock_1_out), .Q(d_ff_34_q), .reset(r));  // open: Qn, preset
  D_Flip_Flop d_ff_35 (.D(d_ff_19_q), .clk(clock_1_out), .Q(d_ff_35_q), .reset(r));  // open: Qn, preset
  D_Flip_Flop d_ff_36 (.D(d_ff_20_q), .clk(clock_1_out), .Q(d_ff_36_q), .reset(r));  // open: Qn, preset
  D_Flip_Flop d_ff_37 (.D(d_ff_21_q), .clk(clock_1_out), .Q(d_ff_37_q), .reset(r));  // open: Qn, preset
  D_Flip_Flop d_ff_38 (.D(d_ff_22_q), .clk(clock_1_out), .Q(d_ff_38_q), .reset(r));  // open: Qn, preset
  D_Flip_Flop d_ff_39 (.D(d_ff_23_q), .clk(clock_1_out), .Q(d_ff_39_q), .reset(r));  // open: Qn, preset
  D_Flip_Flop d_ff_40 (.D(d_ff_24_q), .clk(clock_1_out), .Q(d_ff_40_q), .reset(r));  // open: Qn, preset
  D_Flip_Flop d_ff_41 (.D(d_ff_25_q), .clk(clock_1_out), .Q(d_ff_41_q), .reset(r));  // open: Qn, preset
  D_Flip_Flop d_ff_42 (.D(d_ff_26_q), .clk(clock_1_out), .Q(d_ff_42_q), .reset(r));  // open: Qn, preset
  D_Flip_Flop d_ff_43 (.D(d_ff_27_q), .clk(clock_1_out), .Q(d_ff_43_q), .reset(r));  // open: Qn, preset
  D_Flip_Flop d_ff_44 (.D(d_ff_28_q), .clk(clock_1_out), .Q(d_ff_44_q), .reset(r));  // open: Qn, preset
  D_Flip_Flop d_ff_45 (.D(d_ff_29_q), .clk(clock_1_out), .Q(d_ff_45_q), .reset(r));  // open: Qn, preset
  D_Flip_Flop d_ff_46 (.D(d_ff_30_q), .clk(clock_1_out), .Q(d_ff_46_q), .reset(r));  // open: Qn, preset
  D_Flip_Flop d_ff_47 (.D(d_ff_31_q), .clk(clock_1_out), .Q(d_ff_47_q), .reset(r));  // open: Qn, preset
  D_Flip_Flop d_ff_48 (.D(d_ff_32_q), .clk(clock_1_out), .Q(d_ff_48_q), .reset(r));  // open: Qn, preset
  D_Flip_Flop d_ff_49 (.D(d_ff_33_q), .clk(clock_1_out), .Q(d_ff_49_q), .reset(r));  // open: Qn, preset
  D_Flip_Flop d_ff_50 (.D(d_ff_34_q), .clk(clock_1_out), .Q(d_ff_50_q), .reset(r));  // open: Qn, preset
  D_Flip_Flop d_ff_51 (.D(d_ff_35_q), .clk(clock_1_out), .Q(d_ff_51_q), .reset(r));  // open: Qn, preset
  D_Flip_Flop d_ff_52 (.D(d_ff_36_q), .clk(clock_1_out), .Q(d_ff_52_q), .reset(r));  // open: Qn, preset
  D_Flip_Flop d_ff_53 (.D(d_ff_37_q), .clk(clock_1_out), .Q(d_ff_53_q), .reset(r));  // open: Qn, preset
  D_Flip_Flop d_ff_54 (.D(d_ff_38_q), .clk(clock_1_out), .Q(d_ff_54_q), .reset(r));  // open: Qn, preset
  D_Flip_Flop d_ff_55 (.D(d_ff_39_q), .clk(clock_1_out), .Q(d_ff_55_q), .reset(r));  // open: Qn, preset
  D_Flip_Flop d_ff_56 (.D(d_ff_40_q), .clk(clock_1_out), .Q(d_ff_56_q), .reset(r));  // open: Qn, preset
  D_Flip_Flop d_ff_57 (.D(d_ff_41_q), .clk(clock_1_out), .Q(d_ff_57_q), .reset(r));  // open: Qn, preset
  D_Flip_Flop d_ff_58 (.D(d_ff_42_q), .clk(clock_1_out), .Q(d_ff_58_q), .reset(r));  // open: Qn, preset
  D_Flip_Flop d_ff_59 (.D(d_ff_43_q), .clk(clock_1_out), .Q(d_ff_59_q), .reset(r));  // open: Qn, preset
  D_Flip_Flop d_ff_60 (.D(d_ff_44_q), .clk(clock_1_out), .Q(d_ff_60_q), .reset(r));  // open: Qn, preset
  D_Flip_Flop d_ff_61 (.D(d_ff_45_q), .clk(clock_1_out), .Q(d_ff_61_q), .reset(r));  // open: Qn, preset
  D_Flip_Flop d_ff_62 (.D(d_ff_46_q), .clk(clock_1_out), .Q(d_ff_62_q), .reset(r));  // open: Qn, preset
  D_Flip_Flop d_ff_63 (.D(d_ff_47_q), .clk(clock_1_out), .Q(d_ff_63_q), .reset(r));  // open: Qn, preset
  D_Flip_Flop d_ff_64 (.D(d_ff_48_q), .clk(clock_1_out), .Q(d_ff_64_q), .reset(r));  // open: Qn, preset
  Clock clock_1 (.out(clock_1_out));
  D_Flip_Flop d_ff_65 (.D(d_ff_64_q), .clk(clock_1_out), .Q(d_ff_65_q), .reset(r));  // open: Qn, preset
  D_Flip_Flop d_ff_66 (.D(d_ff_113_q), .clk(clock_1_out), .Q(d_ff_66_q), .reset(r));  // open: Qn, preset
  D_Flip_Flop d_ff_67 (.D(d_ff_114_q), .clk(clock_1_out), .Q(d_ff_67_q), .reset(r));  // open: Qn, preset
  D_Flip_Flop d_ff_68 (.D(d_ff_115_q), .clk(clock_1_out), .Q(d_ff_68_q), .reset(r));  // open: Qn, preset
  D_Flip_Flop d_ff_69 (.D(d_ff_116_q), .clk(clock_1_out), .Q(d_ff_69_q), .reset(r));  // open: Qn, preset
  D_Flip_Flop d_ff_70 (.D(d_ff_117_q), .clk(clock_1_out), .Q(d_ff_70_q), .reset(r));  // open: Qn, preset
  D_Flip_Flop d_ff_71 (.D(d_ff_118_q), .clk(clock_1_out), .Q(d_ff_71_q), .reset(r));  // open: Qn, preset
  D_Flip_Flop d_ff_72 (.D(d_ff_119_q), .clk(clock_1_out), .Q(d_ff_72_q), .reset(r));  // open: Qn, preset
  D_Flip_Flop d_ff_73 (.D(d_ff_120_q), .clk(clock_1_out), .Q(d_ff_73_q), .reset(r));  // open: Qn, preset
  D_Flip_Flop d_ff_74 (.D(d_ff_121_q), .clk(clock_1_out), .Q(d_ff_74_q), .reset(r));  // open: Qn, preset
  D_Flip_Flop d_ff_75 (.D(d_ff_122_q), .clk(clock_1_out), .Q(d_ff_75_q), .reset(r));  // open: Qn, preset
  D_Flip_Flop d_ff_76 (.D(d_ff_123_q), .clk(clock_1_out), .Q(d_ff_76_q), .reset(r));  // open: Qn, preset
  D_Flip_Flop d_ff_77 (.D(d_ff_124_q), .clk(clock_1_out), .Q(d_ff_77_q), .reset(r));  // open: Qn, preset
  D_Flip_Flop d_ff_78 (.D(d_ff_125_q), .clk(clock_1_out), .Q(d_ff_78_q), .reset(r));  // open: Qn, preset
  D_Flip_Flop d_ff_79 (.D(d_ff_126_q), .clk(clock_1_out), .Q(d_ff_79_q), .reset(r));  // open: Qn, preset
  D_Flip_Flop d_ff_80 (.D(d_ff_127_q), .clk(clock_1_out), .Q(d_ff_80_q));  // open: Qn, preset, reset
  D_Flip_Flop d_ff_81 (.D(d_ff_65_q), .clk(clock_1_out), .Q(d_ff_81_q), .reset(r));  // open: Qn, preset
  D_Flip_Flop d_ff_82 (.D(d_ff_66_q), .clk(clock_1_out), .Q(d_ff_82_q), .reset(r));  // open: Qn, preset
  D_Flip_Flop d_ff_83 (.D(d_ff_67_q), .clk(clock_1_out), .Q(d_ff_83_q), .reset(r));  // open: Qn, preset
  D_Flip_Flop d_ff_84 (.D(d_ff_68_q), .clk(clock_1_out), .Q(d_ff_84_q), .reset(r));  // open: Qn, preset
  D_Flip_Flop d_ff_85 (.D(d_ff_69_q), .clk(clock_1_out), .Q(d_ff_85_q), .reset(r));  // open: Qn, preset
  D_Flip_Flop d_ff_86 (.D(d_ff_70_q), .clk(clock_1_out), .Q(d_ff_86_q), .reset(r));  // open: Qn, preset
  D_Flip_Flop d_ff_87 (.D(d_ff_71_q), .clk(clock_1_out), .Q(d_ff_87_q), .reset(r));  // open: Qn, preset
  D_Flip_Flop d_ff_88 (.D(d_ff_72_q), .clk(clock_1_out), .Q(d_ff_88_q), .reset(r));  // open: Qn, preset
  D_Flip_Flop d_ff_89 (.D(d_ff_73_q), .clk(clock_1_out), .Q(d_ff_89_q), .reset(r));  // open: Qn, preset
  D_Flip_Flop d_ff_90 (.D(d_ff_74_q), .clk(clock_1_out), .Q(d_ff_90_q), .reset(r));  // open: Qn, preset
  D_Flip_Flop d_ff_91 (.D(d_ff_75_q), .clk(clock_1_out), .Q(d_ff_91_q), .reset(r));  // open: Qn, preset
  D_Flip_Flop d_ff_92 (.D(d_ff_76_q), .clk(clock_1_out), .Q(d_ff_92_q), .reset(r));  // open: Qn, preset
  D_Flip_Flop d_ff_93 (.D(d_ff_77_q), .clk(clock_1_out), .Q(d_ff_93_q), .reset(r));  // open: Qn, preset
  D_Flip_Flop d_ff_94 (.D(d_ff_78_q), .clk(clock_1_out), .Q(d_ff_94_q), .reset(r));  // open: Qn, preset
  D_Flip_Flop d_ff_95 (.D(d_ff_79_q), .clk(clock_1_out), .Q(d_ff_95_q), .reset(r));  // open: Qn, preset
  D_Flip_Flop d_ff_96 (.D(d_ff_80_q), .clk(clock_1_out), .Q(d_ff_96_q));  // open: Qn, preset, reset
  D_Flip_Flop d_ff_97 (.D(d_ff_81_q), .clk(clock_1_out), .Q(d_ff_97_q), .reset(r));  // open: Qn, preset
  D_Flip_Flop d_ff_98 (.D(d_ff_82_q), .clk(clock_1_out), .Q(d_ff_98_q), .reset(r));  // open: Qn, preset
  D_Flip_Flop d_ff_99 (.D(d_ff_83_q), .clk(clock_1_out), .Q(d_ff_99_q), .reset(r));  // open: Qn, preset
  D_Flip_Flop d_ff_100 (.D(d_ff_84_q), .clk(clock_1_out), .Q(d_ff_100_q), .reset(r));  // open: Qn, preset
  D_Flip_Flop d_ff_101 (.D(d_ff_85_q), .clk(clock_1_out), .Q(d_ff_101_q), .reset(r));  // open: Qn, preset
  D_Flip_Flop d_ff_102 (.D(d_ff_86_q), .clk(clock_1_out), .Q(d_ff_102_q), .reset(r));  // open: Qn, preset
  D_Flip_Flop d_ff_103 (.D(d_ff_87_q), .clk(clock_1_out), .Q(d_ff_103_q), .reset(r));  // open: Qn, preset
  D_Flip_Flop d_ff_104 (.D(d_ff_88_q), .clk(clock_1_out), .Q(d_ff_104_q), .reset(r));  // open: Qn, preset
  D_Flip_Flop d_ff_105 (.D(d_ff_89_q), .clk(clock_1_out), .Q(d_ff_105_q), .reset(r));  // open: Qn, preset
  D_Flip_Flop d_ff_106 (.D(d_ff_90_q), .clk(clock_1_out), .Q(d_ff_106_q), .reset(r));  // open: Qn, preset
  D_Flip_Flop d_ff_107 (.D(d_ff_91_q), .clk(clock_1_out), .Q(d_ff_107_q), .reset(r));  // open: Qn, preset
  D_Flip_Flop d_ff_108 (.D(d_ff_92_q), .clk(clock_1_out), .Q(d_ff_108_q), .reset(r));  // open: Qn, preset
  D_Flip_Flop d_ff_109 (.D(d_ff_93_q), .clk(clock_1_out), .Q(d_ff_109_q), .reset(r));  // open: Qn, preset
  D_Flip_Flop d_ff_110 (.D(d_ff_94_q), .clk(clock_1_out), .Q(d_ff_110_q), .reset(r));  // open: Qn, preset
  D_Flip_Flop d_ff_111 (.D(d_ff_95_q), .clk(clock_1_out), .Q(d_ff_111_q), .reset(r));  // open: Qn, preset
  D_Flip_Flop d_ff_112 (.D(d_ff_96_q), .clk(clock_1_out), .Q(d_ff_112_q));  // open: Qn, preset, reset
  D_Flip_Flop d_ff_113 (.D(d_ff_97_q), .clk(clock_1_out), .Q(d_ff_113_q), .reset(r));  // open: Qn, preset
  D_Flip_Flop d_ff_114 (.D(d_ff_98_q), .clk(clock_1_out), .Q(d_ff_114_q), .reset(r));  // open: Qn, preset
  D_Flip_Flop d_ff_115 (.D(d_ff_99_q), .clk(clock_1_out), .Q(d_ff_115_q), .reset(r));  // open: Qn, preset
  D_Flip_Flop d_ff_116 (.D(d_ff_100_q), .clk(clock_1_out), .Q(d_ff_116_q), .reset(r));  // open: Qn, preset
  D_Flip_Flop d_ff_117 (.D(d_ff_101_q), .clk(clock_1_out), .Q(d_ff_117_q), .reset(r));  // open: Qn, preset
  D_Flip_Flop d_ff_118 (.D(d_ff_102_q), .clk(clock_1_out), .Q(d_ff_118_q), .reset(r));  // open: Qn, preset
  D_Flip_Flop d_ff_119 (.D(d_ff_103_q), .clk(clock_1_out), .Q(d_ff_119_q), .reset(r));  // open: Qn, preset
  D_Flip_Flop d_ff_120 (.D(d_ff_104_q), .clk(clock_1_out), .Q(d_ff_120_q), .reset(r));  // open: Qn, preset
  D_Flip_Flop d_ff_121 (.D(d_ff_105_q), .clk(clock_1_out), .Q(d_ff_121_q), .reset(r));  // open: Qn, preset
  D_Flip_Flop d_ff_122 (.D(d_ff_106_q), .clk(clock_1_out), .Q(d_ff_122_q), .reset(r));  // open: Qn, preset
  D_Flip_Flop d_ff_123 (.D(d_ff_107_q), .clk(clock_1_out), .Q(d_ff_123_q), .reset(r));  // open: Qn, preset
  D_Flip_Flop d_ff_124 (.D(d_ff_108_q), .clk(clock_1_out), .Q(d_ff_124_q), .reset(r));  // open: Qn, preset
  D_Flip_Flop d_ff_125 (.D(d_ff_109_q), .clk(clock_1_out), .Q(d_ff_125_q), .reset(r));  // open: Qn, preset
  D_Flip_Flop d_ff_126 (.D(d_ff_110_q), .clk(clock_1_out), .Q(d_ff_126_q), .reset(r));  // open: Qn, preset
  D_Flip_Flop d_ff_127 (.D(d_ff_111_q), .clk(clock_1_out), .Q(d_ff_127_q), .reset(r));  // open: Qn, preset
  D_Flip_Flop d_ff_128 (.D(d_ff_112_q), .clk(clock_1_out), .Q(r), .Qn(d_ff_128_qn));  // open: preset, reset
  LED LED_1 (.in(r));

  // Notes on the sheet:
  //   16
  //   32
  //   48
  //   64
endmodule

module seven (
  input  [3:0] Input_bus_1,
  output cen,
  output l_h,
  output top,
  output r_h,
  output r_b,
  output bot,
  output l_b
);

  wire nand_1_out, nand_2_out, nand_3_out, nand_4_out, nand_5_out, nand_6_out, nand_7_out, nand_8_out,
       nand_9_out, nand_10_out, nand_11_out, nand_12_out, nand_13_out, nand_14_out, nand_15_out, nand_16_out,
       nand_17_out, nand_18_out, nand_19_out, nand_20_out, nand_21_out, nand_22_out, nand_23_out,
       nand_24_out, nand_25_out, nand_26_out, nand_27_out, nand_28_out, nand_29_out, nand_30_out,
       nand_31_out, nand_32_out, nand_33_out, nand_34_out, nand_35_out, nand_36_out, nand_37_out,
       nand_38_out, nand_39_out, nand_40_out, nand_41_out, nand_42_out, nand_43_out, nand_44_out,
       nand_45_out, nand_46_out, nand_47_out, nand_48_out, nand_49_out, nand_50_out, nand_51_out,
       nand_52_out, nand_53_out, nand_54_out, nand_55_out, nand_56_out, nand_57_out, nand_58_out,
       nand_59_out, nand_60_out, nand_61_out, nand_62_out, nand_63_out, nand_64_out, nand_65_out,
       nand_66_out, nand_67_out, nand_68_out, nand_69_out, nand_70_out, nand_71_out, nand_72_out;

  nand nand_1 (nand_1_out, Input_bus_1[2], Input_bus_1[2]);
  nand nand_2 (nand_2_out, Input_bus_1[1], Input_bus_1[1]);
  nand nand_3 (nand_3_out, Input_bus_1[0], Input_bus_1[0]);
  nand nand_4 (nand_4_out, Input_bus_1[1], Input_bus_1[1]);
  nand nand_5 (nand_5_out, Input_bus_1[0], Input_bus_1[0]);
  nand nand_6 (nand_6_out, Input_bus_1[3], Input_bus_1[3]);
  nand nand_7 (nand_7_out, Input_bus_1[1], Input_bus_1[1]);
  nand nand_8 (nand_8_out, Input_bus_1[0], Input_bus_1[0]);
  nand nand_9 (nand_9_out, Input_bus_1[2], Input_bus_1[2]);
  nand nand_10 (nand_10_out, Input_bus_1[2], Input_bus_1[2]);
  nand nand_11 (nand_11_out, Input_bus_1[0], Input_bus_1[0]);
  nand nand_12 (nand_12_out, Input_bus_1[3], Input_bus_1[3]);
  nand nand_13 (nand_13_out, Input_bus_1[3], Input_bus_1[3]);
  nand nand_14 (nand_14_out, Input_bus_1[2], Input_bus_1[2]);
  nand nand_15 (nand_15_out, Input_bus_1[1], Input_bus_1[1]);
  nand nand_16 (nand_16_out, Input_bus_1[0], Input_bus_1[0]);
  nand nand_17 (nand_17_out, Input_bus_1[3], Input_bus_1[3]);
  nand nand_18 (nand_18_out, Input_bus_1[2], Input_bus_1[2]);
  nand nand_19 (nand_19_out, Input_bus_1[3], Input_bus_1[3]);
  nand nand_20 (nand_20_out, Input_bus_1[1], Input_bus_1[1]);
  nand nand_21 (nand_21_out, Input_bus_1[0], Input_bus_1[0]);
  nand nand_22 (nand_22_out, Input_bus_1[2], Input_bus_1[2]);
  nand nand_23 (nand_23_out, Input_bus_1[0], Input_bus_1[0]);
  nand nand_24 (nand_24_out, Input_bus_1[1], Input_bus_1[1]);
  nand nand_25 (nand_25_out, Input_bus_1[3], Input_bus_1[3]);
  nand nand_26 (nand_26_out, Input_bus_1[1], Input_bus_1[1]);
  nand nand_27 (nand_27_out, Input_bus_1[3], Input_bus_1[3]);
  nand nand_28 (nand_28_out, Input_bus_1[2], Input_bus_1[2]);
  nand nand_29 (nand_29_out, Input_bus_1[3], Input_bus_1[3]);
  nand nand_30 (nand_30_out, Input_bus_1[2], Input_bus_1[2]);
  nand nand_31 (nand_31_out, Input_bus_1[0], Input_bus_1[0]);
  nand nand_32 (nand_32_out, Input_bus_1[2], Input_bus_1[2]);
  nand nand_33 (nand_33_out, Input_bus_1[1], Input_bus_1[1]);
  nand nand_34 (nand_34_out, Input_bus_1[0], Input_bus_1[0]);
  nand nand_35 (nand_35_out, Input_bus_1[1], Input_bus_1[1]);
  nand nand_36 (nand_36_out, Input_bus_1[2], Input_bus_1[2]);
  nand nand_37 (nand_37_out, Input_bus_1[0], Input_bus_1[0]);
  nand nand_38 (nand_38_out, Input_bus_1[0], Input_bus_1[0]);
  nand nand_39 (nand_39_out, Input_bus_1[2], Input_bus_1[2]);
  nand nand_40 (nand_40_out, Input_bus_1[1], Input_bus_1[1]);
  nand nand_41 (nand_41_out, nand_1_out, Input_bus_1[1]);
  nand nand_42 (nand_42_out, Input_bus_1[2], nand_2_out);
  nand nand_43 (nand_43_out, Input_bus_1[2], nand_3_out);
  nand nand_44 (nand_44_out, Input_bus_1[3], Input_bus_1[3]);
  nand nand_45 (nand_45_out, nand_4_out, nand_5_out);
  nand nand_46 (nand_46_out, nand_6_out, Input_bus_1[2], nand_7_out);
  nand nand_47 (nand_47_out, Input_bus_1[2], nand_8_out);
  nand nand_48 (nand_48_out, Input_bus_1[3], nand_9_out);
  nand nand_49 (nand_49_out, nand_10_out, nand_11_out);
  nand nand_50 (nand_50_out, nand_12_out, Input_bus_1[1]);
  nand nand_51 (nand_51_out, nand_13_out, Input_bus_1[2], Input_bus_1[0]);
  nand nand_52 (nand_52_out, Input_bus_1[2], Input_bus_1[1]);
  nand nand_53 (nand_53_out, Input_bus_1[3], nand_14_out, nand_15_out);
  nand nand_54 (nand_54_out, Input_bus_1[3], nand_16_out);
  nand nand_55 (nand_55_out, nand_17_out, nand_18_out);
  nand nand_56 (nand_56_out, nand_19_out, nand_20_out, nand_21_out);
  nand nand_57 (nand_57_out, nand_22_out, nand_23_out);
  nand nand_58 (nand_58_out, Input_bus_1[2], Input_bus_1[1], Input_bus_1[0]);
  nand nand_59 (nand_59_out, Input_bus_1[3], nand_24_out, Input_bus_1[0]);
  nand nand_60 (nand_60_out, nand_25_out, nand_26_out);
  nand nand_61 (nand_61_out, Input_bus_1[0], Input_bus_1[0]);
  nand nand_62 (nand_62_out, nand_27_out, Input_bus_1[2]);
  nand nand_63 (nand_63_out, Input_bus_1[3], nand_28_out);
  nand nand_64 (nand_64_out, nand_29_out, nand_30_out, nand_31_out);
  nand nand_65 (nand_65_out, nand_32_out, Input_bus_1[1], Input_bus_1[0]);
  nand nand_66 (nand_66_out, Input_bus_1[2], nand_33_out, Input_bus_1[0]);
  nand nand_67 (nand_67_out, Input_bus_1[2], Input_bus_1[1], nand_34_out);
  nand nand_68 (nand_68_out, Input_bus_1[3], nand_35_out);
  nand nand_69 (nand_69_out, nand_36_out, nand_37_out);
  nand nand_70 (nand_70_out, Input_bus_1[1], nand_38_out);
  nand nand_71 (nand_71_out, Input_bus_1[3], nand_39_out, Input_bus_1[1]);
  nand nand_72 (nand_72_out, Input_bus_1[3], Input_bus_1[2], nand_40_out);
  nand nand_73 (cen, nand_41_out, nand_42_out, nand_43_out, nand_44_out);
  nand nand_74 (l_h, nand_45_out, nand_46_out, nand_47_out, nand_48_out);
  nand nand_75 (top, nand_49_out, nand_50_out, nand_51_out, nand_52_out, nand_53_out, nand_54_out);
  nand nand_76 (r_h, nand_55_out, nand_56_out, nand_57_out, nand_58_out, nand_59_out);
  nand nand_77 (r_b, nand_60_out, nand_61_out, nand_62_out, nand_63_out);
  nand nand_78 (bot, nand_64_out, nand_65_out, nand_66_out, nand_67_out, nand_68_out);
  nand nand_79 (l_b, nand_69_out, nand_70_out, nand_71_out, nand_72_out);
endmodule

module chron (
  input  R,
  input  EN
);

  count_10 count_10_1 ();  // open: EN, R, data_o, c_out

  // Other names for the same wires on the sheet: A = R; C = EN
endmodule

module button_to_digital (
  input  ONE,
  input  TWO
);


  // Notes on the sheet:
  //   ONE is the A button
  //   ONE + TWO is the B button
  //   TWO is the C button
endmodule

module count_128 (
  input  EN,
  input  R,
  output c
);

  wire and_1_out, and_2_out, and_3_out, and_4_out, and_5_out, clock_1_out, j_k_ff_1_q, j_k_ff_2_q,
       j_k_ff_3_q, j_k_ff_4_q, j_k_ff_5_q, j_k_ff_6_q, or_1_out;

  Clock clock_1 (.out(clock_1_out));
  or or_1 (or_1_out, R, c);
  J_K_Flip_Flop j_k_ff_1 (.J(EN), .K(EN), .clk(clock_1_out), .Q(j_k_ff_1_q), .reset(or_1_out));  // open: Qn, preset
  J_K_Flip_Flop j_k_ff_2 (
    .J(j_k_ff_1_q), .K(j_k_ff_1_q), .clk(clock_1_out), .Q(j_k_ff_2_q), .reset(or_1_out));  // open: Qn, preset
  and and_1 (and_1_out, j_k_ff_2_q, j_k_ff_1_q);
  J_K_Flip_Flop j_k_ff_3 (
    .J(and_1_out), .K(and_1_out), .clk(clock_1_out), .Q(j_k_ff_3_q), .reset(or_1_out));  // open: Qn, preset
  and and_2 (and_2_out, j_k_ff_3_q, and_1_out);
  J_K_Flip_Flop j_k_ff_4 (
    .J(and_2_out), .K(and_2_out), .clk(clock_1_out), .Q(j_k_ff_4_q), .reset(or_1_out));  // open: Qn, preset
  and and_3 (and_3_out, j_k_ff_4_q, and_2_out);
  J_K_Flip_Flop j_k_ff_5 (
    .J(and_3_out), .K(and_3_out), .clk(clock_1_out), .Q(j_k_ff_5_q), .reset(or_1_out));  // open: Qn, preset
  and and_4 (and_4_out, j_k_ff_5_q, and_3_out);
  J_K_Flip_Flop j_k_ff_6 (
    .J(and_4_out), .K(and_4_out), .clk(clock_1_out), .Q(j_k_ff_6_q), .reset(or_1_out));  // open: Qn, preset
  and and_5 (and_5_out, j_k_ff_6_q, and_4_out);
  J_K_Flip_Flop j_k_ff_7 (.J(and_5_out), .K(and_5_out), .clk(clock_1_out), .Q(c));  // open: Qn, preset, reset
endmodule
